// Logisim project lab1.circ as structural Verilog: 5 circuits, main circuit main
module main (
  input  in_1,
  output out_2
);

  // MTH mth_1: pin names not known; wires that end beside it: in_1, out_2
endmodule

module ALU (
  input  math_selector,
  input  in_2,
  input  in_3,
  input  in_4,
  input  in_5,
  input  in_6,
  input  in_7,
  input  in_8,
  input  in_9,
  input  logic_selector,
  input  mode,
  output [3:0] out_12
);

  wire [3:0] LOGIC_out_10, MATH_out_10;

  MTH MATH (
    .in_1(in_2), .in_2(in_3), .in_3(in_4), .in_4(in_5), .in_5(in_6), .in_6(in_7), .in_7(in_8), .in_8(in_9),
    .add_sub_selector(math_selector), .out_10(MATH_out_10));
  LOGIC LOGIC (
    .in_1(in_2), .in_2(in_3), .in_3(in_4), .in_4(in_5), .in_5(in_6), .in_6(in_7), .in_7(in_8), .in_8(in_9),
    .AND_OR(logic_selector), .out_10(LOGIC_out_10));
  Multiplexer #(.width(4), .enable("false")) multiplexer_1 (
    .in0(MATH_out_10), .in1(LOGIC_out_10), .out(out_12), .sel(mode));
endmodule

module MTH (
  input  in_1,
  input  in_2,
  input  in_3,
  input  in_4,
  input  in_5,
  input  in_6,
  input  in_7,
  input  in_8,
  input  add_sub_selector,
  output [3:0] out_10
);

  wire [3:0] adder_1_out, subtractor_1_out;

  Adder #(.width(4)) adder_1 (
    .a({in_1, in_2, in_3, in_4}), .b({in_5, in_6, in_7, in_8}), .out(adder_1_out));  // open: cin, cout
  Subtractor #(.width(4)) subtractor_1 (
    .a({in_1, in_2, in_3, in_4}), .b({in_5, in_6, in_7, in_8}), .out(subtractor_1_out));  // open: bin, bout
  Multiplexer #(.width(4), .enable("false")) multiplexer_1 (
    .in0(adder_1_out), .in1(subtractor_1_out), .out(out_10), .sel(add_sub_selector));
endmodule

module LOGIC (
  input  in_1,
  input  in_2,
  input  in_3,
  input  in_4,
  input  in_5,
  input  in_6,
  input  in_7,
  input  in_8,
  input  AND_OR,
  output [3:0] out_10
);

  wire [3:0] and_1_out, or_1_out;

  assign and_1_out = {in_1, in_2, in_3, in_4} & {in_5, in_6, in_7, in_8};  // AND_Gate and_1, 4 bits wide
  assign or_1_out = {in_1, in_2, in_3, in_4} | {in_5, in_6, in_7, in_8};  // OR_Gate or_1, 4 bits wide
  Multiplexer #(.width(4), .enable("false")) multiplexer_1 (
    .in0(and_1_out), .in1(or_1_out), .out(out_10), .sel(AND_OR));
endmodule

module \reg  (
  input  \readéwrite ,
  input  in_2,
  input  in_3,
  input  in_4,
  input  in_5,
  input  in_6,
  input  in_7,
  input  in_8,
  input  in_9,
  output [3:0] out_10
);

  wire clock_1_out;
  wire [3:0] ALU_out_12, register_1_q, register_2_q;

  Clock clock_1 (.out(clock_1_out));
  ALU ALU (
    .in_2(register_1_q[0]), .in_3(register_1_q[1]), .in_4(register_1_q[2]), .in_5(register_1_q[3]),
    .in_6(register_2_q[0]), .in_7(register_2_q[1]), .in_8(register_2_q[2]), .in_9(register_2_q[3]),
    .out_12(ALU_out_12));  // open: math_selector, logic_selector, mode
  Register #(.width(4)) register_1 (
    .D({in_2, in_3, in_4, in_5}), .en(\readéwrite ), .Q(register_1_q), .clk(clock_1_out));  // open: clr
  Register #(.width(4)) register_2 (
    .D({in_6, in_7, in_8, in_9}), .en(\readéwrite ), .Q(register_2_q), .clk(clock_1_out));  // open: clr
  Register #(.width(4)) register_3 (.D(ALU_out_12), .en(\readéwrite ), .Q(out_10));  // open: clk, clr
endmodule
